# Fritzing sketch schematic (saved by Fritzing 0.9.3b)
breadboards: 1

parts:
  Gizwits_WiFi_Witty_ESP-12F1 = Gizwits WiFi Witty ESP-12F
  D1 = Diode [package=diode-1n4001]
  S1 = SWITCH-MOMENTARY-2 [package=tactile-switch-1101ne]
  R1 = Resistor [tolerance=±5% resistance=220 package=THT]
  C1 = Electrolytic Capacitor [capacitance=1µF package="100 mil [THT, electrolytic]"]
  D2 = Diode [package=diode-1n4001]

nets:
  N1: Gizwits_WiFi_Witty_ESP-12F1.REST, Gizwits_WiFi_Witty_ESP-12F1.GPIO16, D1.A
  N2: Gizwits_WiFi_Witty_ESP-12F1.GPIO12, R1.Pin_1, C1.+, D2.A
  N3: D1.C, S1.2, D2.C
  GND: S1.1, C1.-
  5V: R1.Pin_0
