# Fritzing sketch schematic (saved by Fritzing 0.9.3b)
breadboards: 1

parts:
  WeMos_D1_Mini_Micro_SD_Shield1 = WeMos D1 Mini Micro SD Shield
  R1 = Resistor [tolerance=±5% resistance=470 package="2010 [SMD]"]
  R2 = Resistor [tolerance=±5% resistance=1k package="2010 [SMD]"]
  R3 = Resistor [tolerance=±5% resistance=10k package="2010 [SMD]"]
  S1 = Momentary Switch [package=ksa_sealed_tac_switch]
  C1 = Ceramic Capacitor [capacitance=10µ package="0805 [SMD, multilayer]"]

nets:
  N1: WeMos_D1_Mini_Micro_SD_Shield1.3V3, R3.Pin_1
  N2: WeMos_D1_Mini_Micro_SD_Shield1.D0, R1.Pin_1
  N3: WeMos_D1_Mini_Micro_SD_Shield1.D6, R2.Pin_1
  GND: WeMos_D1_Mini_Micro_SD_Shield1.G, S1.3
  N4: WeMos_D1_Mini_Micro_SD_Shield1.RST, C1.1
  N5: R2.Pin_0, R3.Pin_0, S1.1, C1.0
