# Fritzing sketch schematic (saved by Fritzing 0.9.3b)
breadboards: 1

parts:
  Gizwits_WiFi_Witty_ESP-12F1 = Gizwits WiFi Witty ESP-12F
  Part1 = Adafruit Si7021 Temp Humidity [part_number="Adafruit #3251"]
  VCC1 = Battery

nets:
  VCC: Gizwits_WiFi_Witty_ESP-12F1.VCC, Part1.VIN, VCC1.+
  GND: Gizwits_WiFi_Witty_ESP-12F1.GND, Part1.GND, VCC1.-
  N1: Gizwits_WiFi_Witty_ESP-12F1.GPIO4, Part1.SDA
  N2: Gizwits_WiFi_Witty_ESP-12F1.GPIO5, Part1.SCL

custom parts:
  Adafruit Si7021 Temp Humidity: It's summer and you're sweating and your hair's all frizzy and all you really want to know is why the weatherman said this morning that today's relative humidity would max out at a perfectly reasonable 42% when it feels more like 77%. Enter the Si7021 Temperature + Humidity Sensor - the best way to prove the weatherman wrong! This lovely sensor for Silicon labs has ± 3% relative humidity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
