# Fritzing sketch schematic (saved by Fritzing 0.9.3b)
breadboards: 1

parts:
  Gizwits_WiFi_Witty_ESP-12F1 = Gizwits WiFi Witty ESP-12F
  U1 = 74HC595 SMD [package="SO16 [SMD]"]
  D1 = LTE-302 [package=lte-302]
  VCC1 = 4 x AAA Battery Mount
  D2 = LTE-302 [package=lte-302]
  D3 = LTE-302 [package=lte-302]
  D4 = LTE-302 [package=lte-302]
  D5 = LTE-302 [package=lte-302]

nets:
  N1: Gizwits_WiFi_Witty_ESP-12F1.GPIO14, U1.SH_CP
  N2: Gizwits_WiFi_Witty_ESP-12F1.GPIO13, U1.DS
  N3: Gizwits_WiFi_Witty_ESP-12F1.VCC, VCC1.+
  N4: Gizwits_WiFi_Witty_ESP-12F1.GND, U1.OE, D5.C
  N5: Gizwits_WiFi_Witty_ESP-12F1.GPIO15, U1.ST_CP
  N6: U1.Q1, D1.A
  N7: U1.Q2, D3.A
  N8: U1.Q3, D2.A
  N9: U1.Q4, D2.C, D4.A
  N10: U1.Q5, D5.A
  N11: U1.GND, D1.C
